# Fritzing sketch Circuit_for_Motors (saved by Fritzing 0.9.4)
breadboards: 1

parts:
  元件1 = Arduino Mega 2560 (Rev3)
  J1 = Basic Servo
  M1 = Stepper Motor - Bipolar
  R2 = Trimmer Potentiometer [maximum_resistance=10kΩ package=THT]
  R3 = Resistor [tolerance=±5% resistance=220 package=THT]
  R4 = Resistor [tolerance=±5% resistance=220 package=THT]
  R5 = Resistor [tolerance=±5% resistance=220 package=THT]
  LED1 = LED - 5mm [color="Red (633nm)" package="5 mm [THT]"]
  LED2 = LED - 5mm [color="Blue (505nm)" package="5 mm [THT]"]
  LED3 = LED - 5mm [color="Orange (605nm)" package="5 mm [THT]"]
  S1 = Pushbutton [package="[THT]"]
  R6 = Resistor [tolerance=±5% resistance=10k package=THT]

nets:
  N1: 元件1.A0, R2.wiper
  GND: 元件1.GND, J1.gnd, R2.leg2, LED1.cathode, LED2.cathode, LED3.cathode, R6.Pin_1
  5V: 元件1.5V, J1.vcc, R2.leg1, S1.Pin_3, S1.Pin_4
  N2: 元件1.D2_PWM, M1.D
  N3: 元件1.D3_PWM, M1.B
  N4: 元件1.D4_PWM, M1.C
  N5: 元件1.D5_PWM, M1.A
  N6: 元件1.D6_PWM, J1.pulse
  N7: 元件1.D7_PWM, S1.Pin_1, S1.Pin_2, R6.Pin_0
  N8: 元件1.D23, R3.Pin_1
  N9: 元件1.D25, R4.Pin_1
  N10: 元件1.D27, R5.Pin_1
  N11: R3.Pin_0, LED3.anode
  N12: R4.Pin_0, LED2.anode
  N13: R5.Pin_0, LED1.anode
